// Logisim project S2-T18-Logisim.circ as structural Verilog: 4 circuits, main circuit main
module main (
  input  P1_MSB,
  input  in_2,
  input  in_3,
  input  P1_LSB,
  input  Motion_Sensor,
  input  P1_MSB_2,
  input  in_7,
  input  in_8,
  input  P1_LSB_2,
  input  P1_MSB_3,
  input  in_11,
  input  in_12,
  input  P1_LSB_3,
  input  P1_MSB_4,
  input  in_15,
  input  in_16,
  input  P1_LSB_4,
  input  P1_MSB_5,
  input  in_19,
  input  Fire_Detector,
  input  in_21,
  input  P1_LSB_5,
  input  P1_MSB_6,
  input  in_24,
  input  in_25,
  input  P1_LSB_6,
  input  Fire_Alarm,
  input  Light,
  input  Fan,
  input  AC,
  input  Fan_Speed_MSB,
  input  Fan_Speed_LSB,
  output [3:0] Fan_2
);

  wire AC_t, and_1_out, and_2_out, and_3_out, and_4_out, and_5_out, and_6_out,
       bcd_to_7_segment_decoder_1_a_2, bcd_to_7_segment_decoder_1_b_2, bcd_to_7_segment_decoder_1_c_2,
       bcd_to_7_segment_decoder_1_d_2, bcd_to_7_segment_decoder_1_e, bcd_to_7_segment_decoder_1_f,
       bcd_to_7_segment_decoder_1_g, bcd_to_7_segment_decoder_2_a_2, bcd_to_7_segment_decoder_2_b_2,
       bcd_to_7_segment_decoder_2_c_2, bcd_to_7_segment_decoder_2_d_2, bcd_to_7_segment_decoder_2_e,
       bcd_to_7_segment_decoder_2_f, bcd_to_7_segment_decoder_2_g, bcd_to_7_segment_decoder_3_a_2,
       bcd_to_7_segment_decoder_3_b_2, bcd_to_7_segment_decoder_3_c_2, bcd_to_7_segment_decoder_3_d_2,
       bcd_to_7_segment_decoder_3_e, bcd_to_7_segment_decoder_3_f, bcd_to_7_segment_decoder_3_g,
       decoder_1_y0, Fire_Alarm_t, Light_t, n1_pin_comparator_1_correct, n1_pin_comparator_1_invalid,
       n1_pin_comparator_1_invalid_2, n1_pin_comparator_2_correct, n1_pin_comparator_2_invalid,
       n1_pin_comparator_2_invalid_2, n1_pin_comparator_3_correct, n1_pin_comparator_3_invalid,
       n1_pin_comparator_3_invalid_2, or_1_out, or_2_out, or_3_out, or_4_out, or_5_out, or_6_out;

  LED Invalid (.in(n1_pin_comparator_1_invalid));
  _1_Pin_Comparator u_1_pin_comparator_1 (
    .A3(P1_MSB), .A2(in_2), .A1(in_3), .A0(P1_LSB), .B3(P1_MSB_2), .B2(in_7), .B1(in_8), .B0(P1_LSB_2),
    .Invalid(n1_pin_comparator_1_invalid), .Correct(n1_pin_comparator_1_correct),
    .Invalid_2(n1_pin_comparator_1_invalid_2));
  LED Invalid_2 (.in(n1_pin_comparator_1_invalid_2));
  BCD_to_7_segment_decoder bcd_to_7_segment_decoder_1 (
    .A(P1_MSB_2), .B(in_7), .C(in_8), .D(P1_LSB_2), .a_2(bcd_to_7_segment_decoder_1_a_2),
    .b_2(bcd_to_7_segment_decoder_1_b_2), .c_2(bcd_to_7_segment_decoder_1_c_2),
    .d_2(bcd_to_7_segment_decoder_1_d_2), .e(bcd_to_7_segment_decoder_1_e), .f(bcd_to_7_segment_decoder_1_f),
    .g(bcd_to_7_segment_decoder_1_g));
  LED Invalid_3 (.in(n1_pin_comparator_2_invalid));
  _1_Pin_Comparator u_1_pin_comparator_2 (
    .A3(P1_MSB_3), .A2(in_11), .A1(in_12), .A0(P1_LSB_3), .B3(P1_MSB_4), .B2(in_15), .B1(in_16),
    .B0(P1_LSB_4), .Invalid(n1_pin_comparator_2_invalid), .Correct(n1_pin_comparator_2_correct),
    .Invalid_2(n1_pin_comparator_2_invalid_2));
  LED Invalid_4 (.in(n1_pin_comparator_2_invalid_2));
  BCD_to_7_segment_decoder bcd_to_7_segment_decoder_2 (
    .A(P1_MSB_4), .B(in_15), .C(in_16), .D(P1_LSB_4), .a_2(bcd_to_7_segment_decoder_2_a_2),
    .b_2(bcd_to_7_segment_decoder_2_b_2), .c_2(bcd_to_7_segment_decoder_2_c_2),
    .d_2(bcd_to_7_segment_decoder_2_d_2), .e(bcd_to_7_segment_decoder_2_e), .f(bcd_to_7_segment_decoder_2_f),
    .g(bcd_to_7_segment_decoder_2_g));
  LED Invalid_5 (.in(n1_pin_comparator_3_invalid));
  _1_Pin_Comparator u_1_pin_comparator_3 (
    .A3(P1_MSB_5), .A2(in_19), .A1(in_21), .A0(P1_LSB_5), .B3(P1_MSB_6), .B2(in_24), .B1(in_25),
    .B0(P1_LSB_6), .Invalid(n1_pin_comparator_3_invalid), .Correct(n1_pin_comparator_3_correct),
    .Invalid_2(n1_pin_comparator_3_invalid_2));
  LED Invalid_6 (.in(n1_pin_comparator_3_invalid_2));
  BCD_to_7_segment_decoder bcd_to_7_segment_decoder_3 (
    .A(P1_MSB_6), .B(in_24), .C(in_25), .D(P1_LSB_6), .a_2(bcd_to_7_segment_decoder_3_a_2),
    .b_2(bcd_to_7_segment_decoder_3_b_2), .c_2(bcd_to_7_segment_decoder_3_c_2),
    .d_2(bcd_to_7_segment_decoder_3_d_2), .e(bcd_to_7_segment_decoder_3_e), .f(bcd_to_7_segment_decoder_3_f),
    .g(bcd_to_7_segment_decoder_3_g));
  _7_Segment_Display u_7_segment_display_1 (
    .g(bcd_to_7_segment_decoder_1_g), .f(bcd_to_7_segment_decoder_1_f), .a(bcd_to_7_segment_decoder_1_a_2),
    .b(bcd_to_7_segment_decoder_1_b_2), .e(bcd_to_7_segment_decoder_1_e), .d(bcd_to_7_segment_decoder_1_d_2),
    .c(bcd_to_7_segment_decoder_1_c_2));  // open: dp
  _7_Segment_Display u_7_segment_display_2 (
    .g(bcd_to_7_segment_decoder_2_g), .f(bcd_to_7_segment_decoder_2_f), .a(bcd_to_7_segment_decoder_2_a_2),
    .b(bcd_to_7_segment_decoder_2_b_2), .e(bcd_to_7_segment_decoder_2_e), .d(bcd_to_7_segment_decoder_2_d_2),
    .c(bcd_to_7_segment_decoder_2_c_2));  // open: dp
  _7_Segment_Display u_7_segment_display_3 (
    .g(bcd_to_7_segment_decoder_3_g), .f(bcd_to_7_segment_decoder_3_f), .a(bcd_to_7_segment_decoder_3_a_2),
    .b(bcd_to_7_segment_decoder_3_b_2), .e(bcd_to_7_segment_decoder_3_e), .d(bcd_to_7_segment_decoder_3_d_2),
    .c(bcd_to_7_segment_decoder_3_c_2));  // open: dp
  and and_1 (and_1_out, n1_pin_comparator_1_correct, n1_pin_comparator_2_correct, n1_pin_comparator_3_correct);
  LED led_1 (.in(and_1_out));
  LED led_2 (.in(Motion_Sensor));
  LED led_3 (.in(Fire_Detector));
  and and_2 (and_2_out, and_1_out, and_1_out, Fire_Alarm);
  LED led_4 (.in(Fire_Alarm));
  LED led_5 (.in(Light));
  LED led_6 (.in(Fan));
  LED led_7 (.in(AC));
  and and_3 (and_3_out, and_1_out, Light);
  and and_4 (and_4_out, and_1_out, decoder_1_y0, Fan);
  and and_5 (and_5_out, Motion_Sensor, and_1_out);
  and and_6 (and_6_out, and_1_out, AC);
  Decoder decoder_1 (
    .X1(Fan_Speed_MSB), .X0(Fan_Speed_LSB), .Y3(Fan_2[1]), .Y2(Fan_2[2]), .Y1(Fan_2[3]), .Y0(decoder_1_y0));
  xor xor_1 (Fan_2[0], and_5_out, and_4_out);
  or or_1 (or_1_out, Fan_2[1], Fan_2[2], decoder_1_y0);
  or or_2 (or_2_out, Fan_2[1], Fan_2[2], Fan_2[3], decoder_1_y0);
  or or_3 (or_3_out, Fan_2[2], Fan_2[1]);
  or or_4 (or_4_out, Fan_2[1], Fan_2[3], decoder_1_y0);
  or or_5 (or_5_out, Fan_2[1], Fan_2[2], decoder_1_y0);
  or or_6 (or_6_out, Fan_2[2], decoder_1_y0);
  LED led_8 (.in(Light_t));
  xor xor_2 (Light_t, and_5_out, and_3_out);
  LED Fan_On_Off (.in(Fan_2[0]));
  xor xor_3 (AC_t, and_5_out, and_6_out);
  LED led_9 (.in(Fire_Alarm_t));
  xor xor_4 (Fire_Alarm_t, Fire_Detector, and_2_out);
  _7_Segment_Display u_7_segment_display_4 (
    .g(or_3_out), .f(decoder_1_y0), .a(or_1_out), .b(or_2_out), .e(or_6_out), .d(or_5_out), .c(or_4_out));  // open: dp
  LED led_10 (.in(AC_t));

  // Notes on the sheet:
  //   Pre-Defined Pin-1
  //   User-Entered Pin-1
  //   Pre-Defined Pin-2
  //   User-Entered Pin-2
  //   Pre-Defined Pin-3
  //   User-Entered Pin-3
  //   4-bit Comparator
  //   4-bit Comparator
  //   4-bit Comparator
  //   3 - Pin Security Lock
  //   Smart Home Automation
  //   Pin-1
  //   Pin-2
  //   Pin-3
  //   Fan Speed Regulation
  //   Remote
  //   Fan Speed
  //   3
  //   2
  //   1
  //   Regulator Using Series of Resistors
  //   LSB - On/Off
  //   Regulator Display
endmodule

module _1_Pin_Comparator (
  input  A3,
  input  A2,
  input  A1,
  input  A0,
  input  B3,
  input  B2,
  input  B1,
  input  B0,
  output Invalid,
  output Correct,
  output Invalid_2
);

  wire and_1_out, and_2_out, and_3_out, and_4_out, xnor_1_out, xnor_2_out, xnor_3_out, xnor_4_out;

  and and_1 (and_1_out, A3, A1);
  and and_2 (and_2_out, A3, A2);
  and and_3 (and_3_out, B2, B3);
  and and_4 (and_4_out, B1, B3);
  or or_1 (Invalid, and_1_out, and_2_out);
  xnor xnor_1 (xnor_1_out, A3, B3);
  xnor xnor_2 (xnor_2_out, A2, B2);
  xnor xnor_3 (xnor_3_out, A1, B1);
  xnor xnor_4 (xnor_4_out, A0, B0);
  or or_2 (Invalid_2, and_3_out, and_4_out);
  and and_5 (Correct, xnor_1_out, xnor_2_out, xnor_3_out, xnor_4_out);

  // Notes on the sheet:
  //   1-Pin Comparator
endmodule

module Decoder (
  input  X1,
  input  X0,
  output Y3,
  output Y2,
  output Y1,
  output Y0
);

  wire not_1_out, not_2_out;

  not not_1 (not_1_out, X1);
  not not_2 (not_2_out, X0);
  and and_1 (Y3, X1, X0);
  and and_2 (Y2, X1, not_2_out);
  and and_3 (Y1, not_1_out, X0);
  and and_4 (Y0, not_1_out, not_2_out);
endmodule

module BCD_to_7_segment_decoder (
  input  A,
  input  B,
  input  C,
  input  D,
  output a_2,
  output b_2,
  output c_2,
  output d_2,
  output e,
  output f,
  output g
);

  wire and_1_out, and_2_out, and_3_out, and_4_out, and_5_out, and_6_out, and_7_out, and_8_out, and_9_out,
       and_10_out, and_11_out, and_12_out, and_13_out, and_14_out, and_15_out, and_16_out, and_17_out,
       and_18_out, and_19_out, and_20_out, and_21_out, and_22_out, and_23_out, and_24_out, and_25_out,
       and_26_out, and_27_out, not_1_out, not_2_out, not_3_out, not_4_out, not_5_out, not_6_out, not_7_out,
       not_8_out, not_9_out, not_10_out, not_11_out, not_12_out, not_13_out, not_14_out, not_15_out,
       not_16_out, not_17_out, not_18_out, not_19_out, not_20_out, not_21_out, not_22_out, not_23_out,
       not_24_out, not_25_out, not_26_out, not_27_out, not_28_out, not_29_out, not_30_out, not_31_out,
       not_32_out, not_33_out, not_34_out, not_35_out, not_36_out, not_37_out, not_38_out, not_39_out,
       not_40_out, not_41_out, not_42_out, not_43_out, not_44_out, not_45_out, not_46_out, not_47_out,
       not_48_out, not_49_out, not_50_out, not_51_out, not_52_out, not_53_out, not_54_out, not_55_out;

  not not_1 (not_1_out, A);
  not not_2 (not_2_out, B);
  not not_3 (not_3_out, D);
  not not_4 (not_4_out, A);
  not not_5 (not_5_out, A);
  not not_6 (not_6_out, B);
  not not_7 (not_7_out, C);
  not not_8 (not_8_out, A);
  and and_1 (and_1_out, not_8_out, not_9_out, not_9_out);
  not not_9 (not_9_out, B);
  not not_10 (not_10_out, A);
  not not_11 (not_11_out, C);
  not not_12 (not_12_out, D);
  not not_13 (not_13_out, B);
  not not_14 (not_14_out, C);
  not not_15 (not_15_out, A);
  not not_16 (not_16_out, B);
  not not_17 (not_17_out, C);
  not not_18 (not_18_out, A);
  and and_2 (and_2_out, not_18_out, D);
  not not_19 (not_19_out, A);
  and and_3 (and_3_out, not_19_out, B);
  not not_20 (not_20_out, A);
  not not_21 (not_21_out, B);
  not not_22 (not_22_out, D);
  not not_23 (not_23_out, A);
  not not_24 (not_24_out, B);
  not not_25 (not_25_out, A);
  not not_26 (not_26_out, D);
  not not_27 (not_27_out, A);
  not not_28 (not_28_out, C);
  not not_29 (not_29_out, B);
  not not_30 (not_30_out, C);
  not not_31 (not_31_out, A);
  not not_32 (not_32_out, B);
  not not_33 (not_33_out, D);
  not not_34 (not_34_out, B);
  not not_35 (not_35_out, C);
  not not_36 (not_36_out, D);
  not not_37 (not_37_out, A);
  not not_38 (not_38_out, D);
  not not_39 (not_39_out, A);
  not not_40 (not_40_out, C);
  not not_41 (not_41_out, D);
  not not_42 (not_42_out, A);
  not not_43 (not_43_out, C);
  not not_44 (not_44_out, A);
  not not_45 (not_45_out, D);
  not not_46 (not_46_out, B);
  not not_47 (not_47_out, C);
  not not_48 (not_48_out, A);
  not not_49 (not_49_out, B);
  not not_50 (not_50_out, A);
  not not_51 (not_51_out, C);
  not not_52 (not_52_out, A);
  not not_53 (not_53_out, D);
  not not_54 (not_54_out, B);
  not not_55 (not_55_out, C);
  and and_4 (and_4_out, not_1_out, not_2_out, not_3_out);
  and and_5 (and_5_out, not_4_out, C);
  and and_6 (and_6_out, not_5_out, B, D);
  and and_7 (and_7_out, A, not_6_out, not_7_out);
  and and_8 (and_8_out, not_10_out, not_11_out, not_12_out);
  and and_9 (and_9_out, not_13_out, not_14_out);
  and and_10 (and_10_out, not_15_out, C, D);
  and and_11 (and_11_out, not_16_out, not_17_out);
  and and_12 (and_12_out, not_20_out, not_21_out, not_22_out);
  and and_13 (and_13_out, not_23_out, not_24_out, C);
  and and_14 (and_14_out, not_25_out, C, not_26_out);
  and and_15 (and_15_out, not_27_out, B, not_28_out, D);
  and and_16 (and_16_out, A, not_29_out, not_30_out);
  and and_17 (and_17_out, not_31_out, not_32_out, not_33_out);
  and and_18 (and_18_out, not_34_out, not_35_out, not_36_out);
  and and_19 (and_19_out, not_37_out, C, not_38_out);
  and and_20 (and_20_out, not_39_out, not_40_out, not_41_out);
  and and_21 (and_21_out, not_42_out, B, not_43_out);
  and and_22 (and_22_out, not_44_out, B, not_45_out);
  and and_23 (and_23_out, A, not_46_out, not_47_out);
  and and_24 (and_24_out, not_48_out, not_49_out, C);
  and and_25 (and_25_out, not_50_out, B, not_51_out);
  and and_26 (and_26_out, not_52_out, B, not_53_out);
  and and_27 (and_27_out, A, not_54_out, not_55_out);
  or or_1 (a_2, and_4_out, and_5_out, and_6_out, and_7_out);
  or or_2 (b_2, and_1_out, and_8_out, and_9_out, and_10_out);
  or or_3 (c_2, and_11_out, and_2_out, and_3_out);
  or or_4 (d_2, and_12_out, and_13_out, and_14_out, and_15_out, and_16_out);
  or or_5 (e, and_17_out, and_18_out, and_19_out);
  or or_6 (f, and_20_out, and_21_out, and_22_out, and_23_out);
  or or_7 (g, and_24_out, and_25_out, and_26_out, and_27_out);
endmodule
